# Fritzing sketch CircuitoRasp3B (saved by Fritzing 0.9.3b)

parts:
  Raspberry_Pi_1 = Raspberry Pi 3 [part_number=RPI-3-V1.2]
  KY-1 = Keyes Relay [package=THT]
  Part1 = RFID-RC522-v2
  LED1 = LEDs [package=led10mm]
  J1 = Piezo Speaker

nets:
  3V3: Raspberry_Pi_1.3v3, Part1.3.3V
  N1: Raspberry_Pi_1.GIPO20, J1.pin2
  N2: Raspberry_Pi_1.GIPO16, KY-1.ground
  GND: Raspberry_Pi_1.GND, KY-1.power, Part1.GND, J1.pin1
  N3: Raspberry_Pi_1.GIPO24, Part1.RST
  N4: Raspberry_Pi_1.GIPO23, Part1.MISO
  N5: Raspberry_Pi_1.GIPO18, Part1.MOSI
  N6: Raspberry_Pi_1.GIPO15, Part1.SCK
  N7: Raspberry_Pi_1.GIPO14, Part1.SDA
  N8: Raspberry_Pi_1.5V, KY-1.signal
  N9: KY-1.C, LED1.A

notes:
  Tomada

custom parts:
  Keyes Relay: The Keyes 5V relay module is suitable for SCM development, home appliance control. It uses a 5V~12V TIL control signal which can control DC / AC signal.
  RFID-RC522-v2: A simple China made RFID-RC522 Reader; do check the pin labels, as this is a MFRC522 based clone.
  LEDs: LEDs Standard schematic elements and footprints for 5mm, 3mm, 1206, and 0603 sized LEDs. 5mm - Spark Fun Electronics SKU : COM-00529 (and others)
